// Logisim project ex1-gates.circ as structural Verilog: 1 circuit, main circuit main
module main (
  input  in_1,
  input  in_2,
  input  in_3,
  input  in_4,
  input  in_5,
  input  in_6,
  input  in_7,
  input  in_8,
  input  in_9,
  input  in_10,
  input  in_11,
  output out_12,
  output out_13,
  output out_14,
  output out_15,
  output out_16,
  output out_17
);

  wire nand_2_out, nand_3_out, not_1_out, not_2_out, or_1_out, or_2_out, xor_1_out;

  nand nand_1 (out_12, in_1, 1'b1);
  nand nand_2 (nand_2_out, in_2, in_3);
  not not_1 (not_1_out, in_4);
  not not_2 (not_2_out, in_5);
  or or_1 (or_1_out, in_6, in_7);
  or or_2 (or_2_out, in_8, in_9);
  nand nand_3 (nand_3_out, in_8, in_9);
  xor xor_1 (xor_1_out, in_10, in_11);
  not not_3 (out_13, nand_2_out);
  nand nand_4 (out_14, not_1_out, not_2_out);
  not not_4 (out_15, or_1_out);
  and and_1 (out_16, or_2_out, nand_3_out);
  not not_5 (out_17, xor_1_out);

  // Notes on the sheet:
  //   Not
  //   And
  //   Or
  //   Nor
  //   Xor
  //   Xnor
endmodule
