// Logisim project ex2-addition.circ as structural Verilog: 4 circuits, main circuit main
module main (
  input  [7:0] in_1,
  input  in_2,
  input  [7:0] in_3,
  output [7:0] out_4,
  output out_5
);

  Hex_Digit_Display hex_digit_display_1 (.value(in_1[7:4]));  // open: dp
  Hex_Digit_Display hex_digit_display_2 (.value(in_1[3:0]));  // open: dp
  Hex_Digit_Display hex_digit_display_3 (.value(in_3[7:4]));  // open: dp
  Hex_Digit_Display hex_digit_display_4 (.value(in_3[3:0]));  // open: dp
  byteAdd byteadd_1 (.carryIn(in_2), .a(in_1), .b(in_3), .sum(out_4), .carryOut(out_5));
  Hex_Digit_Display hex_digit_display_5 (.value(out_4[7:4]));  // open: dp
  Hex_Digit_Display hex_digit_display_6 (.value(out_4[3:0]));  // open: dp
endmodule

module halfBitAdd (
  input  a,
  input  b,
  output sum,
  output carryOut
);

  xor xor_1 (sum, a, b);
  and and_1 (carryOut, a, b);
endmodule

module bitAdd (
  input  carryIn,
  input  a,
  input  b,
  output sum,
  output carryOut
);

  wire halfbitadd_1_carryout, halfbitadd_1_sum, halfbitadd_2_carryout;

  halfBitAdd halfbitadd_1 (.a(carryIn), .b(a), .sum(halfbitadd_1_sum), .carryOut(halfbitadd_1_carryout));
  halfBitAdd halfbitadd_2 (.a(halfbitadd_1_sum), .b(b), .sum(sum), .carryOut(halfbitadd_2_carryout));
  or or_1 (carryOut, halfbitadd_1_carryout, halfbitadd_2_carryout);
endmodule

module byteAdd (
  input  carryIn,
  input  [7:0] a,
  input  [7:0] b,
  output [7:0] sum,
  output carryOut
);

  wire bitadd_1_carryout, bitadd_2_carryout, bitadd_3_carryout, bitadd_4_carryout, bitadd_5_carryout,
       bitadd_6_carryout, bitadd_7_carryout;

  bitAdd bitadd_1 (.carryIn(carryIn), .a(a[0]), .b(b[0]), .sum(sum[0]), .carryOut(bitadd_1_carryout));
  bitAdd bitadd_2 (.carryIn(bitadd_1_carryout), .a(a[1]), .b(b[1]), .sum(sum[1]), .carryOut(bitadd_2_carryout));
  bitAdd bitadd_3 (.carryIn(bitadd_2_carryout), .a(a[2]), .b(b[2]), .sum(sum[2]), .carryOut(bitadd_3_carryout));
  bitAdd bitadd_4 (.carryIn(bitadd_3_carryout), .a(a[3]), .b(b[3]), .sum(sum[3]), .carryOut(bitadd_4_carryout));
  bitAdd bitadd_5 (.carryIn(bitadd_4_carryout), .a(a[4]), .b(b[4]), .sum(sum[4]), .carryOut(bitadd_5_carryout));
  bitAdd bitadd_6 (.carryIn(bitadd_5_carryout), .a(a[5]), .b(b[5]), .sum(sum[5]), .carryOut(bitadd_6_carryout));
  bitAdd bitadd_7 (.carryIn(bitadd_6_carryout), .a(a[6]), .b(b[6]), .sum(sum[6]), .carryOut(bitadd_7_carryout));
  bitAdd bitadd_8 (.carryIn(bitadd_7_carryout), .a(a[7]), .b(b[7]), .sum(sum[7]), .carryOut(carryOut));
endmodule
