// Logisim project ex3-mux.circ as structural Verilog
module mux2x1 (
  input  x0,
  input  x1,
  input  sel,
  output data
);

  wire and_1_out, and_2_out, not_1_out;

  not not_1 (not_1_out, sel);
  and and_1 (and_1_out, x1, sel);
  and and_2 (and_2_out, x0, not_1_out);
  or or_1 (data, and_2_out, and_1_out);
endmodule

module mux2x8 (
  input  [7:0] x0,
  input  [7:0] x1,
  input  sel,
  output [7:0] data
);

  mux2x1 mux2x1_1 (.x0(x0[0]), .x1(x1[0]), .sel(sel), .data(data[0]));
  mux2x1 mux2x1_2 (.x0(x0[1]), .x1(x1[1]), .sel(sel), .data(data[1]));
  mux2x1 mux2x1_3 (.x0(x0[2]), .x1(x1[2]), .sel(sel), .data(data[2]));
  mux2x1 mux2x1_4 (.x0(x0[3]), .x1(x1[3]), .sel(sel), .data(data[3]));
  mux2x1 mux2x1_5 (.x0(x0[4]), .x1(x1[4]), .sel(sel), .data(data[4]));
  mux2x1 mux2x1_6 (.x0(x0[5]), .x1(x1[5]), .sel(sel), .data(data[5]));
  mux2x1 mux2x1_7 (.x0(x0[6]), .x1(x1[6]), .sel(sel), .data(data[6]));
  mux2x1 mux2x1_8 (.x0(x0[7]), .x1(x1[7]), .sel(sel), .data(data[7]));
endmodule

module mux2x3 (
  input  [2:0] x0,
  input  [2:0] x1,
  input  sel
);

  wire [2:0] mux2x1_1_data;

  mux2x1 mux2x1_1 (.x0(x0[0]), .x1(x1[0]), .sel(sel), .data(mux2x1_1_data[0]));
  mux2x1 mux2x1_2 (.x0(x0[1]), .x1(x1[1]), .sel(sel), .data(mux2x1_1_data[1]));
  mux2x1 mux2x1_3 (.x0(x0[2]), .x1(x1[2]), .sel(sel), .data(mux2x1_1_data[2]));
endmodule

module mux8x8 (
  input  [7:0] x0,
  input  [7:0] x1,
  input  [7:0] x2,
  input  [7:0] x3,
  input  [7:0] x4,
  input  [7:0] x5,
  input  [7:0] x6,
  input  [7:0] x7,
  input  [2:0] sel,
  output [7:0] data
);

  wire [7:0] mux2x8_1_data, mux2x8_2_data, mux2x8_3_data, mux2x8_4_data, mux2x8_5_data, mux2x8_6_data;

  mux2x8 mux2x8_1 (.x0(x0), .x1(x1), .sel(sel[0]), .data(mux2x8_1_data));
  mux2x8 mux2x8_2 (.x0(x2), .x1(x3), .sel(sel[0]), .data(mux2x8_2_data));
  mux2x8 mux2x8_3 (.x0(x4), .x1(x5), .sel(sel[0]), .data(mux2x8_3_data));
  mux2x8 mux2x8_4 (.x0(x6), .x1(x7), .sel(sel[0]), .data(mux2x8_4_data));
  mux2x8 mux2x8_5 (.x0(mux2x8_1_data), .x1(mux2x8_2_data), .sel(sel[1]), .data(mux2x8_5_data));
  mux2x8 mux2x8_6 (.x0(mux2x8_3_data), .x1(mux2x8_4_data), .sel(sel[1]), .data(mux2x8_6_data));
  mux2x8 mux2x8_7 (.x0(mux2x8_5_data), .x1(mux2x8_6_data), .sel(sel[2]), .data(data));
endmodule
