// Logisim project ex4-ALU.circ as structural Verilog
module ALU (
  input  [7:0] a,
  input  [7:0] b,
  input  [15:0] fct,
  output [7:0] result
);

  wire and_2_out, and_3_out, nor_1_out, not_4_out, or_1_out;
  wire [0:0] multiplexer_5_out;
  wire [7:0] adder_1_out, and_1_out, multiplexer_1_out, multiplexer_2_out, multiplexer_3_out, not_1_out,
       not_2_out, not_3_out;

  assign not_1_out = ~a;  // NOT_Gate not_1, 8 bits wide
  assign not_2_out = ~b;  // NOT_Gate not_2, 8 bits wide
  Multiplexer #(.width(8), .enable("false")) multiplexer_1 (
    .in0(a), .in1(not_1_out), .out(multiplexer_1_out), .sel(fct[6]));
  Multiplexer #(.width(8), .enable("false")) multiplexer_2 (
    .in0(b), .in1(not_2_out), .out(multiplexer_2_out), .sel(fct[7]));
  Adder adder_1 (.a(multiplexer_1_out), .b(multiplexer_2_out), .out(adder_1_out), .cin(fct[9]));  // open: cout
  assign and_1_out = multiplexer_1_out & multiplexer_2_out;  // AND_Gate and_1, 8 bits wide
  Multiplexer #(.select(3), .width(8), .enable("false")) multiplexer_3 (
    .in0(adder_1_out), .in1(and_1_out), .in2({{7{1'b0}}, multiplexer_5_out[0]}), .out(multiplexer_3_out),
    .sel(fct[2:0]));  // open: in3, in4, in5, in6, in7
  nor nor_1 (nor_1_out, adder_1_out[0], adder_1_out[1], adder_1_out[2], adder_1_out[3], adder_1_out[4], adder_1_out[5], adder_1_out[6], adder_1_out[7]);
  assign not_3_out = ~multiplexer_3_out;  // NOT_Gate not_3, 8 bits wide
  and and_2 (and_2_out, fct[11], adder_1_out[7]);
  Multiplexer #(.width(8), .enable("false")) multiplexer_4 (
    .in0(multiplexer_3_out), .in1(not_3_out), .out(result), .sel(fct[8]));
  and and_3 (and_3_out, fct[10], nor_1_out);
  or or_1 (or_1_out, and_3_out, and_2_out);
  not not_4 (not_4_out, or_1_out);
  Multiplexer #(.enable("false")) multiplexer_5 (
    .in0(or_1_out), .in1(not_4_out), .out(multiplexer_5_out[0]), .sel(fct[12]));
endmodule
