// Logisim project ex5-register.circ as structural Verilog
module srNand (
  input  s,
  input  r,
  output q,
  output qP
);

  nand nand_1 (q, s, qP);
  nand nand_2 (qP, q, r);
endmodule

module jkFlipFlop (
  input  j,
  input  e,
  input  k,
  output q,
  output qP
);

  wire nand_1_out, nand_2_out;

  nand nand_1 (nand_1_out, j, e);
  nand nand_2 (nand_2_out, e, k);
  srNand srnand_1 (.s(nand_1_out), .r(nand_2_out), .q(q), .qP(qP));
endmodule

module reg1 (
  input  data,
  input  clock,
  input  reinit,
  output result
);

  wire not_1_out, or_1_out;

  not not_1 (not_1_out, data);
  or or_1 (or_1_out, clock, reinit);
  jkFlipFlop jkflipflop_1 (.j(data), .e(or_1_out), .k(not_1_out), .q(result));  // open: qP
endmodule

module reg8 (
  input  [7:0] data,
  input  writeEnable,
  input  [7:0] initData,
  input  reinit,
  input  clock,
  output [7:0] result
);

  wire or_1_out;
  wire [7:0] multiplexer_1_out, multiplexer_2_out;

  Multiplexer #(.width(8), .enable("false")) multiplexer_1 (
    .in0(result), .in1(data), .out(multiplexer_1_out), .sel(writeEnable));
  Multiplexer #(.width(8), .enable("false")) multiplexer_2 (
    .in0(multiplexer_1_out), .in1(initData), .out(multiplexer_2_out), .sel(reinit));
  or or_1 (or_1_out, reinit, clock);
  reg1 reg1_1 (.data(multiplexer_2_out[0]), .clock(or_1_out), .reinit(or_1_out), .result(result[0]));
  reg1 reg1_2 (.data(multiplexer_2_out[1]), .clock(or_1_out), .reinit(or_1_out), .result(result[1]));
  reg1 reg1_3 (.data(multiplexer_2_out[2]), .clock(or_1_out), .reinit(or_1_out), .result(result[2]));
  reg1 reg1_4 (.data(multiplexer_2_out[3]), .clock(or_1_out), .reinit(or_1_out), .result(result[3]));
  reg1 reg1_5 (.data(multiplexer_2_out[4]), .clock(or_1_out), .reinit(or_1_out), .result(result[4]));
  reg1 reg1_6 (.data(multiplexer_2_out[5]), .clock(or_1_out), .reinit(or_1_out), .result(result[5]));
  reg1 reg1_7 (.data(multiplexer_2_out[6]), .clock(or_1_out), .reinit(or_1_out), .result(result[6]));
  reg1 reg1_8 (.data(multiplexer_2_out[7]), .clock(or_1_out), .reinit(or_1_out), .result(result[7]));
endmodule
